# Fritzing sketch sculpton_shield_ver_A (saved by Fritzing 0.7.12b)
breadboards: 1

parts:
  U1 = Arduino Mega
  R1 = Resistor [tolerance=±5% resistance=10k package=THT]
  R2 = Resistor [tolerance=±5% resistance=10k package=THT]
  R3 = Resistor [tolerance=±5% resistance=10k package=THT]
  R4 = Resistor [tolerance=±5% resistance=10k package=THT]
  R5 = Resistor [tolerance=±5% resistance=10k package=THT]
  R6 = Resistor [tolerance=±5% resistance=10k package=THT]
  J3 = Generic male header - 6 pins [package=THT]
  J5 = Generic male header - 3 pins [package=THT]
  J6 = Generic male header - 3 pins [package=THT]
  J7 = Generic male header - 3 pins [package=THT]
  J12 = Generic female header - 6 pins [package=THT]
  J13 = Generic female header - 6 pins [package=THT]
  J18 = Generic male header - 2 pins [package=THT]
  J19 = Generic female header - 4 pins [package=THT]
  J20 = Generic female header - 6 pins [package=THT]
  J21 = Generic female header - 3 pins [package=THT]
  J22 = Generic male header - 4 pins [package=THT]
  J17 = Generic female header - 6 pins [package=THT]

nets:
  N1: U1.AREF, U1.3V3, J19.pin1, J22.pin1
  N2: U1.+5V, J13.pin1, J13.pin2, J13.pin3, J13.pin4, J13.pin5, J13.pin6, J22.pin2
  N3: U1.GND, R1.Pin_1, R2.Pin_1, R3.Pin_1, R4.Pin_1, R5.Pin_1, R6.Pin_1, J19.pin2, J21.pin1, J21.pin2, J21.pin3, J22.pin3, J22.pin4, J17.pin1, J17.pin2, J17.pin3, J17.pin4, J17.pin5, J17.pin6
  N4: U1.A0, R1.Pin_0, J3.pin1, J12.pin1
  N5: U1.A1, R2.Pin_0, J3.pin2, J12.pin2
  N6: U1.A2, R3.Pin_0, J3.pin3, J12.pin3
  N7: U1.A3, R4.Pin_0, J3.pin4, J12.pin4
  N8: U1.A4, R5.Pin_0, J3.pin5, J12.pin5
  N9: U1.A5, R6.Pin_0, J3.pin6, J12.pin6
  N10: U1.D20, J18.pin1, J19.pin3
  N11: U1.D21, J18.pin2, J19.pin4
  N12: U1.D30, J6.pin1, J20.pin1
  N13: U1.D32, J6.pin2, J20.pin2
  N14: U1.D34, J6.pin3, J20.pin3
  N15: U1.D36, J7.pin1, J20.pin4
  N16: U1.D38, J7.pin2, J20.pin5
  N17: U1.D40, J7.pin3, J20.pin6
  N18: U1.A8, J5.pin1
  N19: U1.A9, J5.pin2
  N20: U1.A10, J5.pin3

notes:
  sculpton
