# Fritzing sketch sculpton_arduinoMegaShield_ver_B (saved by Fritzing 0.7.12b)
breadboards: 1

parts:
  J2 = Generic male header - 4 pins [package=THT]
  J4 = Generic male header - 2 pins [package=THT]
  J5 = Generic male header - 6 pins [package=THT]
  J6 = Generic male header - 6 pins [package=THT]
  J9 = Generic male header - 2 pins [package=THT]
  J10 = Generic female header - 6 pins [package=THT]
  R1 = Resistor [tolerance=±5% resistance=10k package=THT]
  R2 = Resistor [tolerance=±5% resistance=10k package=THT]
  R3 = Resistor [tolerance=±5% resistance=10k package=THT]
  R4 = Resistor [tolerance=±5% resistance=10k package=THT]
  J12 = Generic female header - 6 pins [package=THT]
  J13 = Generic female header - 4 pins [package=THT]
  J14 = Generic female header - 2 pins [package=THT]
  R6 = Resistor [tolerance=±5% resistance=10k package=THT]
  R7 = Resistor [tolerance=±5% resistance=10k package=THT]
  J19 = Generic male header - 3 pins [package=THT]
  R12 = Resistor [tolerance=±5% resistance=270 package=THT]
  R13 = Resistor [tolerance=±5% resistance=270 package=THT]
  R14 = Resistor [tolerance=±5% resistance=270 package=THT]
  R15 = Resistor [tolerance=±5% resistance=270 package=THT]
  R16 = Resistor [tolerance=±5% resistance=270 package=THT]
  R17 = Resistor [tolerance=±5% resistance=270 package=THT]
  J18 = Generic male header - 3 pins [package=THT]
  R18 = Resistor [tolerance=±5% resistance=270 package=THT]
  R19 = Resistor [tolerance=±5% resistance=270 package=THT]
  R20 = Resistor [tolerance=±5% resistance=270 package=THT]
  J11 = Generic female header - 6 pins [package=THT]
  J15 = Generic female header - 6 pins [package=THT]
  J21 = Generic male header [package=THT]
  J23 = Generic male header [package=THT]
  J8 = Generic male header - 2 pins [package=THT]
  R21 = Resistor [tolerance=±5% resistance=10k package=THT]
  J3 = Generic male header [package=THT]
  J25 = Generic male header [package=THT]
  J26 = Generic male header [package=THT]
  J27 = Generic male header [package=THT]
  J28 = Generic male header - 3 pins [package=THT]
  U1 = Arduino Mega
  J29 = Generic male header [package=THT]

nets:
  N1: J2.pin1, J13.pin1, J3.pin1, U1.AREF, U1.3V3
  N2: J2.pin2, J12.pin1, J12.pin2, J12.pin3, J12.pin4, J12.pin5, J12.pin6, U1.+5V#18
  N3: J2.pin3, J2.pin4, J9.pin1, J9.pin2, R1.Pin_1, R2.Pin_1, R3.Pin_1, R4.Pin_1, J13.pin2, J14.pin1, J14.pin2, R6.Pin_1, R7.Pin_1, J15.pin1, J15.pin2, J15.pin3, J15.pin4, J15.pin5, J15.pin6, R21.Pin_1, U1.GND, J29.pin1
  N4: J4.pin1, J13.pin3, U1.D20
  N5: J4.pin2, J13.pin4, U1.D21
  N6: J5.pin1, J11.pin1, U1.D30
  N7: J5.pin2, J11.pin2, U1.D32
  N8: J5.pin3, J11.pin3, U1.D34
  N9: J5.pin4, J11.pin4, U1.D36
  N10: J5.pin5, J11.pin5, U1.D38
  N11: J5.pin6, J11.pin6, U1.D40
  N12: J6.pin1, J10.pin1, R1.Pin_0, U1.A0
  N13: J6.pin2, J10.pin2, R2.Pin_0, U1.A1
  N14: J6.pin3, J10.pin3, R3.Pin_0, U1.A2
  N15: J6.pin4, J10.pin4, R4.Pin_0, U1.A3
  N16: J6.pin5, J10.pin5, R7.Pin_0, U1.A4
  N17: J6.pin6, J10.pin6, R6.Pin_0, U1.A5
  N18: J19.pin1, R17.Pin_0
  N19: J19.pin2, R16.Pin_0
  N20: J19.pin3, R15.Pin_0
  N21: R12.Pin_0, J28.pin3
  N22: R12.Pin_1, U1.D2
  N23: R13.Pin_0, J28.pin2
  N24: R13.Pin_1, U1.D3
  N25: R14.Pin_0, J28.pin1
  N26: R14.Pin_1, U1.D4
  N27: R15.Pin_1, U1.D5
  N28: R16.Pin_1, U1.D8
  N29: R17.Pin_1, U1.D9
  N30: J18.pin1, R20.Pin_0
  N31: J18.pin2, R18.Pin_0
  N32: J18.pin3, R19.Pin_0
  N33: R18.Pin_1, U1.D11
  N34: R19.Pin_1, U1.D10
  N35: R20.Pin_1, U1.D12
  N36: J21.pin1, J23.pin1, U1.D28
  N37: J8.pin1, J25.pin1, U1.+5V#80
  N38: J8.pin2, U1.+5V#81
  N39: R21.Pin_0, J26.pin1, J27.pin1, U1.D46

notes:
  rgb led (x3)
  led inside + 4 led
  footswitch
  sculpton
